// Logisim project 4_BITS_REGISTRO.circ as structural Verilog: 1 circuit, main circuit bit 4Register
// 2
module bit_4Register (
  input  [3:0] Q,
  input  RO,
  input  RI,
  input  CLK,
  output [3:0] out_5
);

  wire d_ff_1_q, d_ff_2_q, d_ff_3_q, d_ff_4_q;

  D_Flip_Flop d_ff_1 (.clk(CLK), .D(Q[0]), .Q(d_ff_1_q), .en(RI));  // open: Qn, preset, reset
  D_Flip_Flop d_ff_2 (.clk(CLK), .D(Q[1]), .Q(d_ff_2_q), .en(RI));  // open: Qn, preset, reset
  D_Flip_Flop d_ff_3 (.clk(CLK), .D(Q[2]), .Q(d_ff_3_q), .en(RI));  // open: Qn, preset, reset
  D_Flip_Flop d_ff_4 (.clk(CLK), .D(Q[3]), .Q(d_ff_4_q), .en(RI));  // open: Qn, preset, reset
  assign out_5[0] = RO ? d_ff_1_q : 1'bz;  // Controlled_Buffer controlled_buffer_1
  assign out_5[1] = RO ? d_ff_2_q : 1'bz;  // Controlled_Buffer controlled_buffer_2
  assign out_5[2] = RO ? d_ff_3_q : 1'bz;  // Controlled_Buffer controlled_buffer_3
  assign out_5[3] = RO ? d_ff_4_q : 1'bz;  // Controlled_Buffer controlled_buffer_4

  // Other names for the same wires on the sheet: CLOCK = CLK; R1 = out_5[0]; R4 = out_5[3]; _0 = Q[0]; _1 = Q[1];
  //   _2 = Q[2]; _3 = Q[3]
endmodule
