// Logisim project 8_BITS_REGISTRO.circ as structural Verilog: 1 circuit, main circuit 8bit Register
module _8bit_Register (
  input  [7:0] D,
  input  clock,
  input  RO,
  input  RI,
  output [7:0] Q
);

  wire FF1, FF2, FF3, FF4, FF5, FF6, FF7, FF8;

  D_Flip_Flop d_ff_1 (.clk(clock), .D(D[0]), .Q(FF1), .en(RI));  // open: Qn, preset, reset
  D_Flip_Flop d_ff_2 (.clk(clock), .D(D[1]), .Q(FF2), .en(RI));  // open: Qn, preset, reset
  D_Flip_Flop d_ff_3 (.clk(clock), .D(D[2]), .Q(FF3), .en(RI));  // open: Qn, preset, reset
  D_Flip_Flop d_ff_4 (.clk(clock), .D(D[3]), .Q(FF4), .en(RI));  // open: Qn, preset, reset
  D_Flip_Flop d_ff_5 (.clk(clock), .D(D[4]), .Q(FF5), .en(RI));  // open: Qn, preset, reset
  D_Flip_Flop d_ff_6 (.clk(clock), .D(D[5]), .Q(FF6), .en(RI));  // open: Qn, preset, reset
  D_Flip_Flop d_ff_7 (.clk(clock), .D(D[6]), .Q(FF7), .en(RI));  // open: Qn, preset, reset
  D_Flip_Flop d_ff_8 (.clk(clock), .D(D[7]), .Q(FF8), .en(RI));  // open: Qn, preset, reset
  assign Q[0] = RO ? FF1 : 1'bz;  // Controlled_Buffer controlled_buffer_1
  assign Q[1] = RO ? FF2 : 1'bz;  // Controlled_Buffer controlled_buffer_2
  assign Q[2] = RO ? FF3 : 1'bz;  // Controlled_Buffer controlled_buffer_3
  assign Q[3] = RO ? FF4 : 1'bz;  // Controlled_Buffer controlled_buffer_4
  assign Q[4] = RO ? FF5 : 1'bz;  // Controlled_Buffer controlled_buffer_5
  assign Q[5] = RO ? FF6 : 1'bz;  // Controlled_Buffer controlled_buffer_6
  assign Q[6] = RO ? FF7 : 1'bz;  // Controlled_Buffer controlled_buffer_7
  assign Q[7] = RO ? FF8 : 1'bz;  // Controlled_Buffer controlled_buffer_8
  Pull_Resistor pull_resistor_1 (.node(RO));

  // Other names for the same wires on the sheet: _0 = D[0]; _1 = D[1]; _2 = D[2]; _3 = D[3]; _4 = D[4]; _5 = D[5];
  //   _6 = D[6]; _7 = D[7]
endmodule
