// Logisim project ALU1_8BITS.circ as structural Verilog: 1 circuit, main circuit 8bit ALU
// e
module _8bit_ALU (
  input  [7:0] A,
  input  [7:0] B,
  input  enabel,
  input  [7:0] mode,
  output [7:0] out
);

  wire [3:0] rom_1_data;
  wire [7:0] AND, Deslocador, \Divisão , \Multiplicação , OR, SOMA, SUBT;

  Shifter shifter_1 (.in(A), .\dist (B[2:0]), .out(Deslocador));
  Adder adder_1 (.a(A), .b(B), .out(SOMA));  // open: cin, cout
  Subtractor subtractor_1 (.a(A), .b(B), .out(SUBT));  // open: bin, bout
  Multiplier multiplier_1 (.a(A), .b(B), .out(\Multiplicação ));  // open: cin, cout
  Divider divider_1 (.a(A), .b(B), .out(\Divisão ));  // open: upper, rem
  assign AND = A & B;  // AND_Gate and_1, 8 bits wide
  assign OR = A | B;  // OR_Gate or_1, 8 bits wide
  ROM #(.dataWidth(4)) rom_1 (.addr(mode), .data(rom_1_data));  // open: sel
  Multiplexer #(.select(3), .width(8)) multiplexer_1 (
    .in0(SOMA), .in1(SUBT), .in2(\Multiplicação ), .in3(\Divisão ), .in4(Deslocador), .in5(AND), .in6(OR),
    .out(out), .sel(rom_1_data[2:0]), .en(enabel));  // open: in7
  // Probe on rom_1_data

  // Notes on the sheet:
  //   contents of rom_1 (hex, n*v repeats v):
  //   7*0 1 0 2 0 3 0 4
endmodule
