// Logisim project CPU 8 BITS.circ as structural Verilog: 1 circuit, main circuit TEST0
// Registrador 2
module TEST0 (
);

  wire AI, AO, BI, BO, BUS_J, C_OU, CAR_I, CE, CI, CL, clock_1_out, clock_2_out, clock_3_out, clock_4_out,
       clock_5_out, clock_6_out, clock_7_out, clock_8_out, clock_9_out, clock_10_out, CM_O, CO,
       controlled_buffer_14_out, counter_1_q, CR_I, CR_O, DAR_I, DM_O, DO, DR_I, DR_O, EO, h, HT_bar, r, Sel;
  wire [7:0] _206_CC, Bar_ram2, Barra_4, controlled_buffer_12_out, counter_2_q, n8bit_alu_1_out, OUTPUT,
       ram_1_data, ram_2_data, Ram_Regis, Ram_Registrador, REG7_q, REG8_q, Regis_CC;
  wire [22:22] rom_1_data;

  Clock clock_1 (.out(clock_1_out));
  Clock clock_2 (.out(clock_2_out));
  Clock clock_3 (.out(clock_3_out));
  _8bit_Register Registrador_2 (
    .D({Barra_4[7:1], Barra_4[1]}), .clock(clock_1_out), .RI(DAR_I), .RO(1'b1), .Q(Ram_Regis));
  Clock clock_4 (.out(clock_4_out));
  _8bit_Register u_8bit_register_1 (.D(Barra_4), .clock(clock_2_out), .RI(DR_I), .RO(DR_O), .Q(Barra_4));
  _8bit_Register Registrador (.D(Bar_ram2), .clock(clock_3_out), .RI(CAR_I), .RO(1'b1), .Q(Ram_Registrador));
  Clock clock_5 (.out(clock_5_out));
  Clock clock_6 (.out(clock_6_out));
  RAM ram_1 (.addr(Ram_Regis), .data(ram_1_data), .sel(1'b1));  // open: clk, ld, clr
  RAM ram_2 (.addr(Ram_Registrador), .data(ram_2_data), .sel(1'b1), .clk(clock_5_out), .clr(1'b0));  // open: ld
  _8bit_Register u_8bit_register_2 (.D(Bar_ram2), .clock(clock_6_out), .RI(CR_I), .RO(CR_O), .Q(Regis_CC));
  assign Barra_4 = DM_O ? ram_1_data : 8'bz;  // Controlled_Buffer controlled_buffer_1
  assign Bar_ram2 = CM_O ? ram_2_data : 8'bz;  // Controlled_Buffer controlled_buffer_2
  Pull_Resistor pull_resistor_1 (.node(BUS_J));
  assign Bar_ram2[0] = BUS_J ? Barra_4[0] : 1'bz;  // Controlled_Buffer controlled_buffer_3
  assign Bar_ram2[3] = BUS_J ? Barra_4[3] : 1'bz;  // Controlled_Buffer controlled_buffer_4
  assign Bar_ram2[1] = BUS_J ? Barra_4[1] : 1'bz;  // Controlled_Buffer controlled_buffer_5
  assign Bar_ram2[2] = BUS_J ? Barra_4[2] : 1'bz;  // Controlled_Buffer controlled_buffer_6
  // Probe on Bar_ram2
  // Probe on {Barra_4[0], Barra_4[1], Barra_4[2], Barra_4[3], Barra_4[4], Barra_4[5], Barra_4[6], Barra_4[7]}
  assign Bar_ram2[4] = BUS_J ? Barra_4[4] : 1'bz;  // Controlled_Buffer controlled_buffer_7
  assign Bar_ram2[6] = BUS_J ? Barra_4[6] : 1'bz;  // Controlled_Buffer controlled_buffer_8
  assign Bar_ram2[7] = BUS_J ? Barra_4[7] : 1'bz;  // Controlled_Buffer controlled_buffer_9
  assign Bar_ram2[5] = BUS_J ? Barra_4[5] : 1'bz;  // Controlled_Buffer controlled_buffer_10
  CC cc_1 (.IR_out(Regis_CC), .ROM_in(_206_CC), .HT_bar(HT_bar), .Sel(Sel), .r(r), .h(h));
  Clock clock_7 (.out(clock_7_out));
  assign Barra_4 = DO ? REG8_q : 8'bz;  // Controlled_Buffer controlled_buffer_11
  // Probe on _206_CC
  assign controlled_buffer_12_out = HT_bar ? _206_CC : 8'bz;  // Controlled_Buffer controlled_buffer_12
  Clock clock_8 (.out(clock_8_out));
  Counter #(.width(1), .max('h1)) counter_1 (.Q(counter_1_q), .clk(clock_9_out));  // open: load, D, count, carry, clr
  Clock clock_9 (.out(clock_9_out));
  Clock clock_10 (.out(clock_10_out));
  _8bit_Register REG7 (.D(REG7_q), .clock(clock_10_out), .RI(BI), .RO(BO), .Q(REG7_q));
  _8bit_ALU u_8bit_alu_1 (.out(n8bit_alu_1_out), .A(Barra_4), .B(REG7_q), .enabel(EO), .mode(_206_CC));
  _8bit_Register REG8 (.D(n8bit_alu_1_out), .clock(clock_7_out), .RI(1'b1), .RO(DO), .Q(REG8_q));
  _8bit_Register REGISTRADOR_2_dup2 (
    .D(Barra_4), .clock(clock_8_out), .RI(CI), .RO(CO),
    .Q({Barra_4[0], Barra_4[1], Barra_4[2], Barra_4[3], Barra_4[4], Barra_4[5], Barra_4[6], Barra_4[7]}));
  assign Barra_4 = controlled_buffer_14_out ? counter_2_q : 8'bz;  // Controlled_Buffer controlled_buffer_13
  Counter counter_2 (.load(CL), .D(Barra_4), .count(CE), .Q(counter_2_q), .clk(counter_1_q));  // open: carry, clr
  assign controlled_buffer_14_out = HT_bar ? C_OU : 1'bz;  // Controlled_Buffer controlled_buffer_14
  _8bit_Register REGIS9 (.D(Barra_4), .clock(clock_10_out), .RI(AI), .RO(AO), .Q(Barra_4));
  // Probe on n8bit_alu_1_out
  assign OUTPUT = DO ? REG8_q : 8'bz;  // Controlled_Buffer controlled_buffer_15
  Pull_Resistor pull_resistor_2 (.node(DO));
  ROM #(.dataWidth(24)) rom_1 (
    .addr(controlled_buffer_12_out),
    .data({h, rom_1_data[22], r, Sel, CI, CO, DO, EO, BI, BO, AI, AO, DR_I, DR_O, DM_O, DAR_I, CR_I, CR_O, CM_O, CAR_I, CL, BUS_J, CE, C_OU}));  // open: sel
  not not_1 (HT_bar, rom_1_data[22]);
  Pull_Resistor pull_resistor_3 (.node(controlled_buffer_14_out));
  Pull_Resistor pull_resistor_4 (.node({h, rom_1_data[22], r, Sel, CI, CO, DO, EO, BI, BO, AI, AO, DR_I, DR_O, DM_O, DAR_I, CR_I, CR_O, CM_O, CAR_I, CL, BUS_J, CE, C_OU}));

  // Other names for the same wires on the sheet: Barramento_Cont[7:0] = Barra_4; DD[7:0] = Barra_4;
  //   Ram_Barra[7:0] = Barra_4; Reg3[7:0] = Barra_4; REG6[7:0] = Barra_4; REG7[7:0] = Barra_4; REG8[7:0] = Barra_4;
  //   Reg_61[7:0] = {Barra_4[0], Barra_4[1], Barra_4[2], Barra_4[3], Barra_4[4], Barra_4[5], Barra_4[6], Barra_4[7]};
  //   Barra_Reg_2[7:0] = {Barra_4[7:1], Barra_4[1]}; Barra_Reg[7:0] = Bar_ram2; Reg__Barra_5[7:0] = Bar_ram2

  // Notes on the sheet:
  //   Ram 2
  //   Barramento de Dados 
  //   Barramento de Endereço
  //   ___
  //   CC
  //   ALU
  //   ROM
  //   Contador
  //   contents of rom_1 (hex, n*v repeats v):
  //   100115 100aa0 100540 202202 208202 815000 822002 815000 822002 815000 822002 815000 822002 815000
  //   822002 600000 200408 202402 208402 804100 802202 801100 808202 206002 209002
endmodule
