// Logisim project Circuito.circ as structural Verilog: 1 circuit, main circuit CC
// false
module CC (
  input  [7:0] IR_out,
  input  HT_bar,
  input  Sel,
  input  r,
  input  h,
  output [7:0] ROM_in
);

  wire and_1_out, and_2_out, clock_1_out, clock_2_out, counter_3_q, not_1_out, not_2_out, not_3_out;
  wire [7:0] adder_1_out, counter_1_q, counter_2_q, pull_resistor_1_node, register_1_q;

  Pull_Resistor pull_resistor_1 (.node(pull_resistor_1_node));
  Counter counter_1 (.count(h), .Q(counter_1_q), .clk(clock_1_out));  // open: load, D, carry, clr
  Clock clock_1 (.out(clock_1_out));
  not not_1 (not_1_out, h);
  not not_2 (not_2_out, h);
  and and_1 (and_1_out, not_2_out, not_3_out);
  not not_3 (not_3_out, Sel);
  Clock clock_2 (.out(clock_2_out));
  // Probe on adder_1_out
  Adder adder_1 (.a(counter_1_q), .b(register_1_q), .out(adder_1_out));  // open: cin, cout
  assign pull_resistor_1_node = and_2_out ? IR_out : 8'bz;  // Controlled_Buffer controlled_buffer_1
  and and_2 (and_2_out, not_1_out, HT_bar);
  Register register_1 (.D(pull_resistor_1_node), .Q(register_1_q), .clk(counter_3_q));  // open: en, clr
  assign ROM_in = Sel ? counter_2_q : 8'bz;  // Controlled_Buffer controlled_buffer_2
  Counter counter_2 (.count(Sel), .Q(counter_2_q), .clk(counter_3_q), .clr(r));  // open: load, D, carry
  Counter #(.width(1), .max('h1)) counter_3 (.Q(counter_3_q), .clk(clock_2_out));  // open: load, D, count, carry, clr
  assign ROM_in = h ? adder_1_out : 8'bz;  // Controlled_Buffer controlled_buffer_3
  Pull_Resistor pull_resistor_2 (.node(IR_out));
  assign ROM_in = and_1_out ? register_1_q : 8'bz;  // Controlled_Buffer controlled_buffer_4

  // Notes on the sheet:
  //   Incrementar
  //   h
  //   Sel
  //   Soma
  //   control logic
  //   sub controler
  //   r
endmodule
