// Logisim project Instrucao_registro.circ as structural Verilog: 1 circuit, main circuit instruction_register1
module instruction_register1 (
  input  Alt,
  input  clock,
  input  [7:0] D,
  input  RO,
  input  RI,
  output [7:0] Q
);

  wire FF1, FF2, FF3, FF4, FF5, FF6, FF7, FF8, or_1_out;

  D_Flip_Flop d_ff_1 (.clk(clock), .D(D[0]), .Q(FF1), .en(RI));  // open: Qn, preset, reset
  D_Flip_Flop d_ff_2 (.clk(clock), .D(D[1]), .Q(FF2), .en(RI));  // open: Qn, preset, reset
  D_Flip_Flop d_ff_3 (.clk(clock), .D(D[2]), .Q(FF3), .en(RI));  // open: Qn, preset, reset
  D_Flip_Flop d_ff_4 (.clk(clock), .D(D[3]), .Q(FF4), .en(RI));  // open: Qn, preset, reset
  D_Flip_Flop d_ff_5 (.clk(clock), .D(D[4]), .Q(FF5), .en(RI));  // open: Qn, preset, reset
  D_Flip_Flop d_ff_6 (.clk(clock), .D(D[5]), .Q(FF6), .en(RI));  // open: Qn, preset, reset
  D_Flip_Flop d_ff_7 (.clk(clock), .D(D[6]), .Q(FF7), .en(RI));  // open: Qn, preset, reset
  D_Flip_Flop d_ff_8 (.clk(clock), .D(D[7]), .Q(FF8), .en(RI));  // open: Qn, preset, reset
  or or_1 (or_1_out, Alt, RO);
  assign Q[0] = or_1_out ? FF1 : 1'bz;  // Controlled_Buffer controlled_buffer_1
  assign Q[1] = or_1_out ? FF2 : 1'bz;  // Controlled_Buffer controlled_buffer_2
  assign Q[2] = or_1_out ? FF3 : 1'bz;  // Controlled_Buffer controlled_buffer_3
  assign Q[3] = or_1_out ? FF4 : 1'bz;  // Controlled_Buffer controlled_buffer_4
  assign Q[4] = RO ? FF5 : 1'bz;  // Controlled_Buffer controlled_buffer_5
  assign Q[5] = RO ? FF6 : 1'bz;  // Controlled_Buffer controlled_buffer_6
  assign Q[6] = RO ? FF7 : 1'bz;  // Controlled_Buffer controlled_buffer_7
  assign Q[7] = RO ? FF8 : 1'bz;  // Controlled_Buffer controlled_buffer_8

  // Other names for the same wires on the sheet: OR = RO
endmodule
